# Fritzing sketch AzollaSense (saved by Fritzing 1.0.5)
breadboards: 1

parts:
  U1 = ESP32-38PinWide [part_number=ESP32]
  PH_Sensor = ph-4502c [package=THT]
  Lux_Sensor = TSL2591 Sensor Module
  Ultrasonic_Sensor = JSN-SRO4T [package=THT]
  WATER_PUMP = water pump/motor
  Canopy_Motor_Driver = drv-1012
  Solenoid_Valve = Plastic Solenoid Valve
  Solenoid_Relay = 1 chan 5v relay module
  Water_Pump_Relay = 1 chan 5v relay module
  R1 = Resistor [tolerance=±5% power=0.25W resistance=1k package=THT]
  R2 = Resistor [tolerance=±5% power=0.25W resistance=2k package=THT]
  R3 = Resistor [tolerance=±5% power=0.25W resistance=1k package=THT]
  R4 = Resistor [tolerance=±5% power=0.25W resistance=2k package=THT]
  A1 = Arduino pluggable terminal
  Buck_Convertor1 = Buck Convertor [part_number="5V Buck Converter" package=THT]
  A2 = S-350-60 Power Supply [part_number="12V Power Supply" package=THT]
  A3 = S-350-60 Power Supply [part_number="12V Power Supply" package=THT]
  Buck_Convertor2 = Buck Convertor [part_number="3.3V Buck Converter" package=THT]
  Temperature_Sensor = DS18B20 1-Wire Temperature Sensor Probe
  Canopy_Open_Limiter = CSM405 Camdenboss Snap Action Limit Switch
  Canopy_Closed_Limiter = CSM405 Camdenboss Snap Action Limit Switch
  Canopy_Motor = DC Mini Metal Gear Motor

nets:
  N1: U1.GPIO34, R3.Pin_1
  N2: U1.GPIO32, Canopy_Motor_Driver.Pin_7
  N3: U1.GPIO33, Canopy_Motor_Driver.Pin_3
  N4: U1.GPIO25, Canopy_Motor_Driver.Pin_8
  N5: U1.GPIO26, Canopy_Motor_Driver.Pin_4
  N6: U1.GPIO27, Solenoid_Relay.pin_3
  N7: U1.GPIO14, Water_Pump_Relay.pin_3
  GND: U1.GND, PH_Sensor.pin4, PH_Sensor.pin5, Lux_Sensor.GND, Ultrasonic_Sensor.pin1, WATER_PUMP.pin_2, Canopy_Motor_Driver.Pin_1, Canopy_Motor_Driver.Pin_11, Solenoid_Valve.no_name_yet#2, Solenoid_Relay.pin_2, Water_Pump_Relay.pin_2, R2.Pin_1, R4.Pin_1, A1.Pin_3, A1.Pin_4, Buck_Convertor1.Negative_Output, A3.-V1, A3.-V2, A3.-V3, Buck_Convertor2.Negative_Output, Temperature_Sensor.GND, Canopy_Open_Limiter.Pin_1, Canopy_Closed_Limiter.Pin_1
  N8: U1.GPIO4, A1.Pin_1, A1.Pin_6, Temperature_Sensor.DQ
  N9: U1.GPIO5, Ultrasonic_Sensor.pin3
  N10: U1.GPIO18, R1.Pin_1
  N11: U1.GPIO19, Canopy_Open_Limiter.Pin_2
  N12: U1.GPIO21, Lux_Sensor.SDA
  N13: U1.GPIO22, Lux_Sensor.SCL
  N14: U1.GPIO23, Canopy_Closed_Limiter.Pin_2
  N15: PH_Sensor.pin3, R3.Pin_0, R4.Pin_0
  N16: PH_Sensor.pin6, Ultrasonic_Sensor.pin4, Canopy_Motor_Driver.Pin_5, Solenoid_Relay.pin_1, Water_Pump_Relay.pin_1, Buck_Convertor1.Positive_Output
  VIN: Lux_Sensor.VIN, A1.Pin_2, A1.Pin_5, Buck_Convertor2.Positive_Output, Temperature_Sensor.VDD
  N17: Ultrasonic_Sensor.pin2, R1.Pin_0, R2.Pin_0
  N18: WATER_PUMP.pin_1, Water_Pump_Relay.pin_5
  N19: Canopy_Motor_Driver.Pin_9, Canopy_Motor.IN2
  N20: Canopy_Motor_Driver.Pin_10, Canopy_Motor.IN1
  N21: Canopy_Motor_Driver.Pin_12, Solenoid_Relay.pin_4, Water_Pump_Relay.pin_4, A3.+V1, A3.+V2, A3.+V3
  N22: Solenoid_Valve.no_name_yet#1, Solenoid_Relay.pin_5
  N23: Buck_Convertor1.Negative_Input, A2.-V1, A2.-V2, A2.-V3, Buck_Convertor2.Negative_Input
  N24: Buck_Convertor1.Positive_Input, A2.+V1, A2.+V2, A2.+V3, Buck_Convertor2.Positive_Input

custom parts:
  ESP32-38PinWide: Generic 38-Pin ESP32 with wide format (only access to one side of pins on a breadboard) based on Stephen Lilley's HiLetgo ESP-WROOM-32 ESP32 ESP-32S Development Board.
  ph-4502c: ph-4502c PH Meter.
  TSL2591 Sensor Module: A temperature and humidity sensor.
  JSN-SRO4T: JSN-SR04T Waterproof Ultrasonic Distance Measuring Module Integrated Ultrasonic Detection Module DC 5V.
  water pump/motor: WATER PUMP BY ARDUBLOCKTR
  drv-1012: .The BTS7960 is a fully integrated high current H bridge module for motor drive applications.
  1 chan 5v relay module: 1 Channel 5V Relay Module Board Shield with Optocoupler Support High and Low Level Trigger for Arduino.
  Arduino pluggable terminal: Arduino pluggable terminal.
  Buck Convertor: DC to DC buck convertor
  S-350-60 Power Supply: 350W Stepper motor power supply. June 2024 clean up errors in the part.
  CSM405 Camdenboss Snap Action Limit Switch: Snap action switch with stainless steel lever.
